// Logisim project project.circ as structural Verilog: 1 circuit, main circuit main
module main (
  input  [15:0] lo_en,
  input  [15:0] lo_en_2,
  input  [7:0] sel
);

  wire clk, demultiplexer_1_out0, demultiplexer_1_out1, demultiplexer_1_out2, demultiplexer_1_out3,
       demultiplexer_1_out4, demultiplexer_1_out5, demultiplexer_1_out6, demultiplexer_1_out7,
       demultiplexer_1_out8, demultiplexer_1_out9, demultiplexer_1_out10, demultiplexer_1_out11,
       demultiplexer_1_out12, demultiplexer_1_out13, demultiplexer_1_out14, demultiplexer_1_out15,
       demultiplexer_1_out16, demultiplexer_1_out17, demultiplexer_1_out18, demultiplexer_1_out19,
       demultiplexer_1_out20, demultiplexer_1_out21, demultiplexer_1_out22, demultiplexer_1_out23,
       demultiplexer_1_out24, demultiplexer_1_out25, demultiplexer_1_out26, demultiplexer_1_out27,
       demultiplexer_1_out28, demultiplexer_1_out29, demultiplexer_1_out30, demultiplexer_1_out31, or_1_out;
  wire [7:0] selector_q;
  wire [15:0] lo_2_q, lo_q;
  wire [31:0] register_1_q, register_2_q, register_3_q, register_4_q, register_5_q, register_6_q,
       register_7_q, register_8_q, register_9_q, register_10_q, register_11_q, register_12_q, register_13_q,
       register_14_q, register_15_q, register_16_q, register_17_q, register_18_q, register_19_q,
       register_20_q, register_21_q, register_22_q, register_23_q, register_24_q, register_25_q,
       register_26_q, register_27_q, register_28_q, register_29_q, register_30_q, register_31_q,
       register_32_q;

  Clock clock_1 (.out(clk));
  Register #(.width(16)) lo (.D(lo_en_2), .en(1'b1), .Q(lo_q), .clk(clk));  // open: clr
  Register selector (.D(sel), .en(1'b1), .Q(selector_q), .clk(clk));  // open: clr
  Register #(.width(16)) lo_2 (.D(lo_en), .en(1'b1), .Q(lo_2_q), .clk(clk));  // open: clr
  or or_1 (or_1_out, 1'b1, 1'b1);
  // Probe on selector_q
  Demultiplexer #(.select(5)) demultiplexer_1 (
    .out0(demultiplexer_1_out0), .out1(demultiplexer_1_out1), .out2(demultiplexer_1_out2),
    .out3(demultiplexer_1_out3), .out4(demultiplexer_1_out4), .out5(demultiplexer_1_out5),
    .out6(demultiplexer_1_out6), .out7(demultiplexer_1_out7), .out8(demultiplexer_1_out8),
    .out9(demultiplexer_1_out9), .out10(demultiplexer_1_out10), .out11(demultiplexer_1_out11),
    .out12(demultiplexer_1_out12), .out13(demultiplexer_1_out13), .out14(demultiplexer_1_out14),
    .out15(demultiplexer_1_out15), .out16(demultiplexer_1_out16), .out17(demultiplexer_1_out17),
    .out18(demultiplexer_1_out18), .out19(demultiplexer_1_out19), .out20(demultiplexer_1_out20),
    .out21(demultiplexer_1_out21), .out22(demultiplexer_1_out22), .out23(demultiplexer_1_out23),
    .out24(demultiplexer_1_out24), .out25(demultiplexer_1_out25), .out26(demultiplexer_1_out26),
    .out27(demultiplexer_1_out27), .out28(demultiplexer_1_out28), .out29(demultiplexer_1_out29),
    .out30(demultiplexer_1_out30), .out31(demultiplexer_1_out31), .in(or_1_out), .sel(selector_q[4:0]),
    .en(1'b1));
  Register #(.width(32)) register_1 (
    .D({lo_q, lo_2_q}), .en(demultiplexer_1_out0), .Q(register_1_q), .clk(clk));  // open: clr
  Register #(.width(32)) register_2 (
    .D({lo_q, lo_2_q}), .en(demultiplexer_1_out1), .Q(register_2_q), .clk(clk));  // open: clr
  Register #(.width(32)) register_3 (
    .D({lo_q, lo_2_q}), .en(demultiplexer_1_out2), .Q(register_3_q), .clk(clk));  // open: clr
  Register #(.width(32)) register_4 (
    .D({lo_q, lo_2_q}), .en(demultiplexer_1_out3), .Q(register_4_q), .clk(clk));  // open: clr
  Register #(.width(32)) register_5 (
    .D({lo_q, lo_2_q}), .en(demultiplexer_1_out4), .Q(register_5_q), .clk(clk));  // open: clr
  Register #(.width(32)) register_6 (
    .D({lo_q, lo_2_q}), .en(demultiplexer_1_out5), .Q(register_6_q), .clk(clk));  // open: clr
  Register #(.width(32)) register_7 (
    .D({lo_q, lo_2_q}), .en(demultiplexer_1_out6), .Q(register_7_q), .clk(clk));  // open: clr
  Register #(.width(32)) register_8 (
    .D({lo_q, lo_2_q}), .en(demultiplexer_1_out7), .Q(register_8_q), .clk(clk));  // open: clr
  Register #(.width(32)) register_9 (
    .D({lo_q, lo_2_q}), .en(demultiplexer_1_out8), .Q(register_9_q), .clk(clk));  // open: clr
  Register #(.width(32)) register_10 (
    .D({lo_q, lo_2_q}), .en(demultiplexer_1_out9), .Q(register_10_q), .clk(clk));  // open: clr
  Register #(.width(32)) register_11 (
    .D({lo_q, lo_2_q}), .en(demultiplexer_1_out10), .Q(register_11_q), .clk(clk));  // open: clr
  Register #(.width(32)) register_12 (
    .D({lo_q, lo_2_q}), .en(demultiplexer_1_out11), .Q(register_12_q), .clk(clk));  // open: clr
  Register #(.width(32)) register_13 (
    .D({lo_q, lo_2_q}), .en(demultiplexer_1_out12), .Q(register_13_q), .clk(clk));  // open: clr
  Register #(.width(32)) register_14 (
    .D({lo_q, lo_2_q}), .en(demultiplexer_1_out13), .Q(register_14_q), .clk(clk));  // open: clr
  Register #(.width(32)) register_15 (
    .D({lo_q, lo_2_q}), .en(demultiplexer_1_out14), .Q(register_15_q), .clk(clk));  // open: clr
  Register #(.width(32)) register_16 (
    .D({lo_q, lo_2_q}), .en(demultiplexer_1_out15), .Q(register_16_q), .clk(clk));  // open: clr
  Register #(.width(32)) register_17 (
    .D({lo_q, lo_2_q}), .en(demultiplexer_1_out16), .Q(register_17_q), .clk(clk));  // open: clr
  Register #(.width(32)) register_18 (
    .D({lo_q, lo_2_q}), .en(demultiplexer_1_out17), .Q(register_18_q), .clk(clk));  // open: clr
  Register #(.width(32)) register_19 (
    .D({lo_q, lo_2_q}), .en(demultiplexer_1_out18), .Q(register_19_q), .clk(clk));  // open: clr
  Register #(.width(32)) register_20 (
    .D({lo_q, lo_2_q}), .en(demultiplexer_1_out19), .Q(register_20_q), .clk(clk));  // open: clr
  Register #(.width(32)) register_21 (
    .D({lo_q, lo_2_q}), .en(demultiplexer_1_out20), .Q(register_21_q), .clk(clk));  // open: clr
  Register #(.width(32)) register_22 (
    .D({lo_q, lo_2_q}), .en(demultiplexer_1_out21), .Q(register_22_q), .clk(clk));  // open: clr
  Register #(.width(32)) register_23 (
    .D({lo_q, lo_2_q}), .en(demultiplexer_1_out22), .Q(register_23_q), .clk(clk));  // open: clr
  Register #(.width(32)) register_24 (
    .D({lo_q, lo_2_q}), .en(demultiplexer_1_out23), .Q(register_24_q), .clk(clk));  // open: clr
  Register #(.width(32)) register_25 (
    .D({lo_q, lo_2_q}), .en(demultiplexer_1_out24), .Q(register_25_q), .clk(clk));  // open: clr
  Register #(.width(32)) register_26 (
    .D({lo_q, lo_2_q}), .en(demultiplexer_1_out25), .Q(register_26_q), .clk(clk));  // open: clr
  Register #(.width(32)) register_27 (
    .D({lo_q, lo_2_q}), .en(demultiplexer_1_out26), .Q(register_27_q), .clk(clk));  // open: clr
  Register #(.width(32)) register_28 (
    .D({lo_q, lo_2_q}), .en(demultiplexer_1_out27), .Q(register_28_q), .clk(clk));  // open: clr
  Register #(.width(32)) register_29 (
    .D({lo_q, lo_2_q}), .en(demultiplexer_1_out28), .Q(register_29_q), .clk(clk));  // open: clr
  Register #(.width(32)) register_30 (
    .D({lo_q, lo_2_q}), .en(demultiplexer_1_out29), .Q(register_30_q), .clk(clk));  // open: clr
  Register #(.width(32)) register_31 (
    .D({lo_q, lo_2_q}), .en(demultiplexer_1_out30), .Q(register_31_q), .clk(clk));  // open: clr
  Register #(.width(32)) register_32 (
    .D({lo_q, lo_2_q}), .en(demultiplexer_1_out31), .Q(register_32_q), .clk(clk));  // open: clr
  DotMatrix #(.inputtype("row"), .matrixcols(32), .matrixrows(32)) dotmatrix_1 (
    .row0(register_1_q), .row1(register_2_q), .row2(register_3_q), .row3(register_4_q), .row4(register_5_q),
    .row5(register_6_q), .row6(register_7_q), .row7(register_8_q), .row8(register_9_q), .row9(register_10_q),
    .row10(register_11_q), .row11(register_12_q), .row12(register_13_q), .row13(register_14_q),
    .row14(register_15_q), .row15(register_16_q), .row16(register_17_q), .row17(register_18_q),
    .row18(register_19_q), .row19(register_20_q), .row20(register_21_q), .row21(register_22_q),
    .row22(register_23_q), .row23(register_24_q), .row24(register_25_q), .row25(register_26_q),
    .row26(register_27_q), .row27(register_28_q), .row28(register_29_q), .row29(register_30_q),
    .row30(register_31_q), .row31(register_32_q));
endmodule
